// Logisim project 实验5-CS1805-U201814629-裴涵.circ as structural Verilog
module \四位二进制可逆计数器  (
  input  CPd,
  input  LD,
  input  A,
  input  B,
  input  C,
  input  CLR,
  input  CPu,
  input  D,
  output QA,
  output QB,
  output QC,
  output QD
);

  wire and_1_out, and_2_out, and_3_out, and_4_out, and_5_out, and_6_out, and_7_out, and_8_out, and_9_out,
       and_10_out, and_11_out, and_12_out, and_13_out, and_14_out, d_ff_1_qn, d_ff_2_qn, d_ff_3_qn,
       d_ff_4_qn, or_1_out, or_2_out, or_3_out, or_4_out, or_5_out, or_6_out, or_7_out, or_8_out;

  or or_1 (or_1_out, CPd, CPu);
  and and_1 (and_1_out, d_ff_1_qn, CPd);
  or or_2 (or_2_out, and_1_out, and_2_out);
  and and_2 (and_2_out, CPu, ~d_ff_1_qn);  // AND_Gate
  and and_3 (and_3_out, d_ff_2_qn, d_ff_1_qn, CPd);
  and and_4 (and_4_out, ~d_ff_2_qn, ~d_ff_1_qn, CPu);  // AND_Gate
  and and_5 (and_5_out, d_ff_3_qn, d_ff_2_qn, d_ff_1_qn, CPd);
  and and_6 (and_6_out, ~d_ff_3_qn, ~d_ff_2_qn, ~d_ff_1_qn, CPu);  // AND_Gate
  or or_3 (or_3_out, and_3_out, and_4_out);
  or or_4 (or_4_out, and_5_out, and_6_out);
  D_Flip_Flop #(.trigger("falling"), .Pre_Clr_Positions("LEGACY"), .NegatePresetClear("false"), .enable("true"), .NewFFLayout("false")) d_ff_1 (
    .clk(or_1_out), .D(d_ff_1_qn), .Q(QA), .Qn(d_ff_1_qn), .preset(and_13_out), .reset(or_7_out));  // open: en
  D_Flip_Flop #(.trigger("falling"), .Pre_Clr_Positions("LEGACY"), .NegatePresetClear("false"), .enable("true"), .NewFFLayout("false")) d_ff_2 (
    .clk(or_2_out), .D(d_ff_2_qn), .Q(QB), .Qn(d_ff_2_qn), .preset(and_7_out), .reset(or_5_out));  // open: en
  or or_5 (or_5_out, and_8_out, CLR);
  D_Flip_Flop #(.trigger("falling"), .Pre_Clr_Positions("LEGACY"), .NegatePresetClear("false"), .enable("true"), .NewFFLayout("false")) d_ff_3 (
    .clk(or_3_out), .D(d_ff_3_qn), .Q(QC), .Qn(d_ff_3_qn), .preset(and_10_out), .reset(or_6_out));  // open: en
  or or_6 (or_6_out, and_9_out, CLR);
  D_Flip_Flop #(.trigger("falling"), .Pre_Clr_Positions("LEGACY"), .NegatePresetClear("false"), .enable("true"), .NewFFLayout("false")) d_ff_4 (
    .clk(or_4_out), .D(d_ff_4_qn), .Q(QD), .Qn(d_ff_4_qn), .preset(and_14_out), .reset(or_8_out));  // open: en
  or or_7 (or_7_out, and_12_out, CLR);
  and and_7 (and_7_out, ~LD, ~CLR, B);  // AND_Gate
  and and_8 (and_8_out, ~B, ~LD);  // AND_Gate
  and and_9 (and_9_out, ~LD, ~C);  // AND_Gate
  and and_10 (and_10_out, ~CLR, ~LD, C);  // AND_Gate
  and and_11 (and_11_out, ~LD, ~D);  // AND_Gate
  or or_8 (or_8_out, CLR, and_11_out);
  and and_12 (and_12_out, ~LD, ~A);  // AND_Gate
  and and_13 (and_13_out, A, ~LD, ~CLR);  // AND_Gate
  and and_14 (and_14_out, ~CLR, ~LD, D);  // AND_Gate
endmodule

module \六十进制计数器  (
  input  Adj,
  input  CPd,
  input  CLr,
  input  CPu,
  output out_5,
  output out_6,
  output out_7,
  output out_8,
  output out_9,
  output out_10,
  output out_11,
  output out_12,
  output out_13
);

  wire and_1_out, and_2_out, and_3_out, and_4_out, and_5_out, and_6_out, and_7_out, nand_1_out, or_1_out,
       or_2_out, or_3_out, or_4_out;

  or or_1 (or_1_out, out_8, out_7, out_6, out_5, or_3_out);
  and and_1 (and_1_out, CPd, Adj, or_1_out);
  or or_2 (or_2_out, and_2_out, CLr);
  or or_3 (or_3_out, out_11, out_10, out_9, out_12);
  and and_2 (and_2_out, ~out_11, out_10, ~out_9, out_12);  // AND_Gate
  and and_3 (and_3_out, out_11, out_10, out_9, out_12);
  \四位二进制可逆计数器  \u_四位二进制可逆计数器_1  (
    .CPd(and_1_out), .CPu(CPu), .QA(out_11), .LD(nand_1_out), .A(1'b1), .QB(out_10), .B(1'b0), .QC(out_9),
    .C(1'b0), .CLR(or_2_out), .QD(out_12), .D(1'b1));
  nand nand_1 (nand_1_out, ~CPd, and_3_out);  // NAND_Gate
  and and_4 (and_4_out, and_3_out, ~and_1_out);  // AND_Gate
  or or_4 (or_4_out, CLr, and_5_out);
  and and_5 (and_5_out, ~out_8, out_7, out_6, ~out_5);  // AND_Gate
  \四位二进制可逆计数器  \u_四位二进制可逆计数器_2  (
    .CPd(and_4_out), .CPu(and_2_out), .QA(out_8), .LD(1'b1), .A(1'b1), .QB(out_7), .B(1'b1), .QC(out_6),
    .C(1'b1), .CLR(or_4_out), .QD(out_5), .D(1'b1));
  and and_6 (and_6_out, out_8, ~out_7, out_6, ~out_5, out_11, ~out_10, ~out_9, out_12);  // AND_Gate
  and and_7 (and_7_out, and_6_out, CPu);
  not not_1 (out_13, and_7_out);
endmodule

module \六十进制计数器测试电路  (
  input  in_1,
  input  in_2,
  output out_3
);

  wire button_1_out, button_2_out;
  wire [3:0] \六十进制计数器_1_out_8 , \六十进制计数器_1_out_11 ;

  Button button_1 (.out(button_1_out));
  Button button_2 (.out(button_2_out));
  Hex_Digit_Display hex_digit_display_1 (.value(\六十进制计数器_1_out_8 ));  // open: dp
  Hex_Digit_Display hex_digit_display_2 (.value(\六十进制计数器_1_out_11 ));  // open: dp
  \六十进制计数器  \u_六十进制计数器_1  (
    .Adj(in_1), .CPd(button_2_out), .CLr(in_2), .CPu(button_1_out), .out_13(out_3),
    .out_12(\六十进制计数器_1_out_11 [3]), .out_9(\六十进制计数器_1_out_11 [2]), .out_10(\六十进制计数器_1_out_11 [1]),
    .out_11(\六十进制计数器_1_out_11 [0]), .out_5(\六十进制计数器_1_out_8 [3]), .out_6(\六十进制计数器_1_out_8 [2]),
    .out_7(\六十进制计数器_1_out_8 [1]), .out_8(\六十进制计数器_1_out_8 [0]));
endmodule

module \十二进制计数器或二十四进制的计数器电路  (
  input  in_1,
  input  in_2,
  input  in_3,
  input  in_4,
  input  in_5,
  output out_6,
  output out_7,
  output out_8,
  output out_9,
  output out_10,
  output out_11,
  output out_12,
  output out_13,
  output out_14
);

  wire and_1_out, and_2_out, or_1_out, or_2_out, or_3_out, or_4_out;
  wire [3:0] multiplexer_1_out, multiplexer_2_out, \六十进制计数器_1_out_8 , \六十进制计数器_1_out_11 ;
  wire [7:0] \六十进制计数器_2_out_11 ;

  Multiplexer #(.select(1), .width(4), .disabled("Z"), .enable("false")) multiplexer_1 (
    .in0(4'b0001), .in1(\六十进制计数器_1_out_8 ), .out(multiplexer_1_out), .sel(or_2_out));
  \六十进制计数器  \u_六十进制计数器_1  (
    .Adj(in_3), .CPd(in_4), .CLr(or_1_out), .CPu(in_2), .out_12(\六十进制计数器_1_out_11 [3]),
    .out_9(\六十进制计数器_1_out_11 [2]), .out_10(\六十进制计数器_1_out_11 [1]), .out_11(\六十进制计数器_1_out_11 [0]),
    .out_5(\六十进制计数器_1_out_8 [3]), .out_6(\六十进制计数器_1_out_8 [2]), .out_7(\六十进制计数器_1_out_8 [1]),
    .out_8(\六十进制计数器_1_out_8 [0]));  // open: out_13
  and and_1 (and_1_out, ~\六十进制计数器_1_out_11 [0], \六十进制计数器_1_out_11 [1], ~\六十进制计数器_1_out_11 [2], ~\六十进制计数器_1_out_11 [3], \六十进制计数器_1_out_8 [0]);  // AND_Gate
  or or_1 (or_1_out, and_1_out, in_5);
  or or_2 (or_2_out, \六十进制计数器_1_out_11 [0], \六十进制计数器_1_out_11 [2], \六十进制计数器_1_out_11 [1], \六十进制计数器_1_out_11 [3], \六十进制计数器_1_out_8 [0]);
  Multiplexer #(.select(1), .width(4), .disabled("Z"), .enable("false")) multiplexer_2 (
    .in0(4'b0010), .in1(\六十进制计数器_1_out_11 ), .out(multiplexer_2_out), .sel(or_2_out));
  or or_3 (or_3_out, and_1_out, and_2_out);
  not not_1 (out_14, or_3_out);
  Multiplexer #(.select(1), .width(8), .disabled("Z"), .enable("false")) multiplexer_3 (
    .in0({multiplexer_1_out, multiplexer_2_out}), .in1(\六十进制计数器_2_out_11 ),
    .out({out_6, out_7, out_8, out_9, out_10, out_11, out_12, out_13}), .sel(in_1));
  and and_2 (and_2_out, ~\六十进制计数器_2_out_11 [0], ~\六十进制计数器_2_out_11 [1], \六十进制计数器_2_out_11 [2], ~\六十进制计数器_2_out_11 [3], ~\六十进制计数器_2_out_11 [4], \六十进制计数器_2_out_11 [5]);  // AND_Gate
  \六十进制计数器  \u_六十进制计数器_2  (
    .Adj(in_3), .CPd(in_4), .CLr(or_4_out), .CPu(in_2), .out_12(\六十进制计数器_2_out_11 [3]),
    .out_9(\六十进制计数器_2_out_11 [2]), .out_10(\六十进制计数器_2_out_11 [1]), .out_11(\六十进制计数器_2_out_11 [0]),
    .out_5(\六十进制计数器_2_out_11 [7]), .out_6(\六十进制计数器_2_out_11 [6]), .out_7(\六十进制计数器_2_out_11 [5]),
    .out_8(\六十进制计数器_2_out_11 [4]));  // open: out_13
  or or_4 (or_4_out, and_2_out, in_5);
endmodule

module \十二进制计数器或二十四进制的计数器测试电路  (
  input  in_1,
  input  in_2,
  input  in_3
);

  wire button_1_out, button_2_out, not_1_out, \十二进制计数器或二十四进制的计数器电路_1_out_14 ;
  wire [3:0] \十二进制计数器或二十四进制的计数器电路_1_out_9 , \十二进制计数器或二十四进制的计数器电路_1_out_13 ;

  Button button_1 (.out(button_1_out));
  Button button_2 (.out(button_2_out));
  Hex_Digit_Display hex_digit_display_1 (.value(\十二进制计数器或二十四进制的计数器电路_1_out_9 ));  // open: dp
  Hex_Digit_Display hex_digit_display_2 (.value(\十二进制计数器或二十四进制的计数器电路_1_out_13 ));  // open: dp
  \十二进制计数器或二十四进制的计数器电路  \u_十二进制计数器或二十四进制的计数器电路_1  (
    .out_14(\十二进制计数器或二十四进制的计数器电路_1_out_14 ), .in_2(button_1_out), .in_3(in_1), .in_4(button_2_out),
    .in_5(in_3), .in_1(in_2), .out_6(\十二进制计数器或二十四进制的计数器电路_1_out_9 [3]),
    .out_7(\十二进制计数器或二十四进制的计数器电路_1_out_9 [2]), .out_8(\十二进制计数器或二十四进制的计数器电路_1_out_9 [1]),
    .out_9(\十二进制计数器或二十四进制的计数器电路_1_out_9 [0]), .out_10(\十二进制计数器或二十四进制的计数器电路_1_out_13 [3]),
    .out_11(\十二进制计数器或二十四进制的计数器电路_1_out_13 [2]), .out_12(\十二进制计数器或二十四进制的计数器电路_1_out_13 [1]),
    .out_13(\十二进制计数器或二十四进制的计数器电路_1_out_13 [0]));
  not not_1 (not_1_out, \十二进制计数器或二十四进制的计数器电路_1_out_14 );
  D_Flip_Flop #(.trigger("rising"), .Pre_Clr_Positions("ABOVE_BELOW"), .NegatePresetClear("false"), .enable("false"), .NewFFLayout("true")) d_ff_1 (.preset(not_1_out));  // open: clk, D, Q, Qn, reset
endmodule

module \上下午文字显示的电路  (
  input  AM_TM,
  input  TT,
  output [4:0] out_3,
  output [4:0] out_4,
  output [4:0] out_5,
  output [4:0] out_6
);

  wire [19:0] multiplexer_1_out;

  Multiplexer #(.select(1), .width(20), .disabled("Z"), .enable("false")) multiplexer_1 (
    .in0(20'hfca1), .in1(20'h87e90), .out(multiplexer_1_out), .sel(AM_TM));
  Multiplexer #(.select(1), .width(20), .disabled("Z"), .enable("false")) multiplexer_2 (
    .in0({20{1'b0}}), .in1(multiplexer_1_out), .out({out_6, out_5, out_4, out_3}), .sel(TT));
endmodule

module \上下午文字显示测试电路  (
  input  in_1,
  input  in_2
);

  wire [4:0] \上下午文字显示的电路_1_out_3 , \上下午文字显示的电路_1_out_4 , \上下午文字显示的电路_1_out_5 , \上下午文字显示的电路_1_out_6 ;

  DotMatrix #(.inputtype("column"), .matrixcols(4), .matrixrows(5), .persist(0), .dotshape("square")) dotmatrix_1 (
    .col0(\上下午文字显示的电路_1_out_6 ), .col1(\上下午文字显示的电路_1_out_5 ), .col2(\上下午文字显示的电路_1_out_4 ),
    .col3(\上下午文字显示的电路_1_out_3 ));
  \上下午文字显示的电路  \u_上下午文字显示的电路_1  (
    .out_3(\上下午文字显示的电路_1_out_3 ), .out_4(\上下午文字显示的电路_1_out_4 ), .out_5(\上下午文字显示的电路_1_out_5 ),
    .out_6(\上下午文字显示的电路_1_out_6 ), .AM_TM(in_1), .TT(in_2));
endmodule

module \电子钟整点报时电路  (
  input  in_1,
  input  in_2,
  input  in_3,
  input  in_4,
  input  in_5,
  input  in_6,
  input  in_7,
  input  in_8,
  input  in_9,
  input  in_10,
  input  in_11,
  input  in_12,
  output out_13
);

  wire and_1_out, and_3_out, and_4_out;

  and and_1 (and_1_out, ~in_1, in_2, ~in_3, in_4);  // AND_Gate
  and and_2 (out_13, and_1_out, and_3_out, and_4_out);
  and and_3 (and_3_out, in_5, ~in_6, ~in_7, in_8);  // AND_Gate
  and and_4 (and_4_out, ~in_9, in_10, ~in_11, in_12);  // AND_Gate
endmodule

module \电子钟整点报时电路测试电路  (
  input  set,
  input  Clr,
  input  Adj0,
  input  Adj1
);

  wire and_1_out, and_2_out, and_3_out, and_4_out, and_5_out, and_6_out, button_1_out, button_2_out,
       clock_1_out, multiplexer_1_out, multiplexer_2_out, not_1_out, not_2_out, or_1_out, \六十进制计数器_1_out_13 ,
       \六十进制计数器_2_out_13 , \电子钟整点报时电路_1_out_13 ;
  wire [3:0] \六十进制计数器_1_out_8 , \六十进制计数器_1_out_11 , \六十进制计数器_2_out_8 , \六十进制计数器_2_out_11 ,
       \十二进制计数器或二十四进制的计数器电路_1_out_9 , \十二进制计数器或二十四进制的计数器电路_1_out_13 ;

  Button button_1 (.out(button_1_out));
  Clock #(.highDuration(1), .lowDuration(1)) clock_1 (.out(clock_1_out));
  Button button_2 (.out(button_2_out));
  \六十进制计数器  \u_六十进制计数器_1  (
    .Adj(1'b0), .CPd(1'b0), .CLr(Clr), .CPu(clock_1_out), .out_13(\六十进制计数器_1_out_13 ),
    .out_12(\六十进制计数器_1_out_11 [3]), .out_9(\六十进制计数器_1_out_11 [2]), .out_10(\六十进制计数器_1_out_11 [1]),
    .out_11(\六十进制计数器_1_out_11 [0]), .out_5(\六十进制计数器_1_out_8 [3]), .out_6(\六十进制计数器_1_out_8 [2]),
    .out_7(\六十进制计数器_1_out_8 [1]), .out_8(\六十进制计数器_1_out_8 [0]));
  not not_1 (not_1_out, \六十进制计数器_1_out_13 );
  and and_1 (and_1_out, not_1_out, ~or_1_out);  // AND_Gate
  or or_1 (or_1_out, and_2_out, and_4_out);
  and and_2 (and_2_out, Adj0, Adj1);
  \电子钟整点报时电路  \u_电子钟整点报时电路_1  (
    .out_13(\电子钟整点报时电路_1_out_13 ), .in_1(\六十进制计数器_2_out_8 [3]), .in_2(\六十进制计数器_2_out_8 [2]),
    .in_3(\六十进制计数器_2_out_8 [1]), .in_4(\六十进制计数器_2_out_8 [0]), .in_5(\六十进制计数器_2_out_11 [3]),
    .in_6(\六十进制计数器_2_out_11 [2]), .in_7(\六十进制计数器_2_out_11 [1]), .in_8(\六十进制计数器_2_out_11 [0]),
    .in_9(\六十进制计数器_1_out_8 [3]), .in_10(\六十进制计数器_1_out_8 [2]), .in_11(\六十进制计数器_1_out_8 [1]),
    .in_12(\六十进制计数器_1_out_8 [0]));
  Multiplexer #(.select(1), .width(1), .disabled("Z"), .enable("false")) multiplexer_1 (
    .in0(and_1_out), .in1(button_1_out), .out(multiplexer_1_out), .sel(and_2_out));
  and and_3 (and_3_out, and_2_out, button_2_out);
  and and_4 (and_4_out, Adj0, ~Adj1);  // AND_Gate
  \六十进制计数器  \u_六十进制计数器_2  (
    .Adj(and_2_out), .CPd(and_3_out), .CLr(Clr), .CPu(multiplexer_1_out), .out_13(\六十进制计数器_2_out_13 ),
    .out_12(\六十进制计数器_2_out_11 [3]), .out_9(\六十进制计数器_2_out_11 [2]), .out_10(\六十进制计数器_2_out_11 [1]),
    .out_11(\六十进制计数器_2_out_11 [0]), .out_5(\六十进制计数器_2_out_8 [3]), .out_6(\六十进制计数器_2_out_8 [2]),
    .out_7(\六十进制计数器_2_out_8 [1]), .out_8(\六十进制计数器_2_out_8 [0]));
  LED #(.active("true")) led_1 (.in(\电子钟整点报时电路_1_out_13 ));
  not not_2 (not_2_out, \六十进制计数器_2_out_13 );
  and and_5 (and_5_out, not_2_out, ~or_1_out);  // AND_Gate
  Multiplexer #(.select(1), .width(1), .disabled("Z"), .enable("false")) multiplexer_2 (
    .in0(and_5_out), .in1(button_1_out), .out(multiplexer_2_out), .sel(and_4_out));
  Hex_Digit_Display hex_digit_display_1 (.value(\十二进制计数器或二十四进制的计数器电路_1_out_9 ));  // open: dp
  and and_6 (and_6_out, and_4_out, button_2_out);
  Hex_Digit_Display hex_digit_display_2 (.value(\十二进制计数器或二十四进制的计数器电路_1_out_13 ));  // open: dp
  \十二进制计数器或二十四进制的计数器电路  \u_十二进制计数器或二十四进制的计数器电路_1  (
    .in_2(multiplexer_2_out), .in_3(and_4_out), .in_4(and_6_out), .in_5(Clr), .in_1(set),
    .out_6(\十二进制计数器或二十四进制的计数器电路_1_out_9 [3]), .out_7(\十二进制计数器或二十四进制的计数器电路_1_out_9 [2]),
    .out_8(\十二进制计数器或二十四进制的计数器电路_1_out_9 [1]), .out_9(\十二进制计数器或二十四进制的计数器电路_1_out_9 [0]),
    .out_10(\十二进制计数器或二十四进制的计数器电路_1_out_13 [3]), .out_11(\十二进制计数器或二十四进制的计数器电路_1_out_13 [2]),
    .out_12(\十二进制计数器或二十四进制的计数器电路_1_out_13 [1]), .out_13(\十二进制计数器或二十四进制的计数器电路_1_out_13 [0]));  // open: out_14
  Hex_Digit_Display hex_digit_display_3 (.value(\六十进制计数器_2_out_8 ));  // open: dp
  Hex_Digit_Display hex_digit_display_4 (.value(\六十进制计数器_2_out_11 ));  // open: dp
  Hex_Digit_Display hex_digit_display_5 (.value(\六十进制计数器_1_out_8 ));  // open: dp
  Hex_Digit_Display hex_digit_display_6 (.value(\六十进制计数器_1_out_11 ));  // open: dp

  // Notes on the sheet:
  //   CPu
  //   CPD
endmodule

module \秒脉冲产生电路  (
  input  in_1,
  output out_2
);

  wire \四位二进制可逆计数器_1_qa , \四位二进制可逆计数器_1_qb , \四位二进制可逆计数器_1_qc , \四位二进制可逆计数器_1_qd ;

  and and_1 (out_2, \四位二进制可逆计数器_1_qd , ~\四位二进制可逆计数器_1_qc , ~\四位二进制可逆计数器_1_qb , ~\四位二进制可逆计数器_1_qa );  // AND_Gate
  \四位二进制可逆计数器  \u_四位二进制可逆计数器_1  (
    .CPd(1'b0), .CPu(in_1), .QA(\四位二进制可逆计数器_1_qa ), .LD(1'b1), .A(1'b1), .QB(\四位二进制可逆计数器_1_qb ), .B(1'b1),
    .QC(\四位二进制可逆计数器_1_qc ), .C(1'b1), .CLR(out_2), .QD(\四位二进制可逆计数器_1_qd ), .D(1'b1));
endmodule

module \闹钟  (
  input  [3:0] in_1,
  input  [3:0] in_2,
  input  [3:0] in_3,
  input  [3:0] in_4,
  input  Alarm,
  input  Aset,
  input  in_7,
  input  in_8,
  input  in_9,
  input  in_10,
  input  CPu,
  input  in_12,
  input  CPD,
  input  Clr,
  input  Adj0,
  input  Adj1,
  output [3:0] out_17,
  output [3:0] out_18,
  output [3:0] out_19,
  output [3:0] out_20,
  output out_21
);

  wire and_1_out, and_2_out, and_3_out, and_4_out, and_5_out, or_2_out, or_3_out, xor_5_out, xor_6_out,
       xor_7_out, xor_8_out;
  wire [3:0] or_1_out, xor_1_out, xor_2_out, xor_3_out, xor_4_out;

  and and_1 (and_1_out, CPu, Alarm);
  and and_2 (and_2_out, Alarm, CPD);
  and and_3 (and_3_out, Alarm, Clr);
  and and_4 (and_4_out, Adj0, Alarm, Adj1);
  \六十进制计数器  \u_六十进制计数器_1  (
    .Adj(and_4_out), .CPd(and_2_out), .CLr(and_3_out), .CPu(and_1_out), .out_12(out_18[3]),
    .out_9(out_18[2]), .out_10(out_18[1]), .out_11(out_18[0]), .out_5(out_17[3]), .out_6(out_17[2]),
    .out_7(out_17[1]), .out_8(out_17[0]));  // open: out_13
  and and_5 (and_5_out, Adj0, Alarm, ~Adj1);  // AND_Gate
  \十二进制计数器或二十四进制的计数器电路  \u_十二进制计数器或二十四进制的计数器电路_1  (
    .in_2(and_1_out), .in_3(and_5_out), .in_4(and_2_out), .in_5(and_3_out), .in_1(in_12), .out_6(out_19[3]),
    .out_7(out_19[2]), .out_8(out_19[1]), .out_9(out_19[0]), .out_10(out_20[3]), .out_11(out_20[2]),
    .out_12(out_20[1]), .out_13(out_20[0]));  // open: out_14
  assign xor_1_out = out_17 ^ in_1;  // XOR_Gate xor_1, 4 bits wide
  assign xor_2_out = out_18 ^ in_2;  // XOR_Gate xor_2, 4 bits wide
  assign xor_3_out = out_19 ^ in_3;  // XOR_Gate xor_3, 4 bits wide
  assign xor_4_out = out_20 ^ in_4;  // XOR_Gate xor_4, 4 bits wide
  assign or_1_out = xor_1_out | xor_2_out | xor_3_out | xor_4_out;  // OR_Gate or_1, 4 bits wide
  xor xor_5 (xor_5_out, or_1_out[0], 1'b0);
  xor xor_6 (xor_6_out, 1'b0, or_1_out[1]);
  xor xor_7 (xor_7_out, 1'b0, or_1_out[2]);
  xor xor_8 (xor_8_out, 1'b0, or_1_out[3]);
  or or_2 (or_2_out, xor_5_out, xor_6_out, xor_7_out, xor_8_out);
  or or_3 (or_3_out, in_7, in_8, in_9, in_10);
  and and_6 (out_21, ~or_2_out, ~or_3_out, Aset);  // AND_Gate
endmodule
