// Logisim project 实验6-CS1805-U201814629-裴涵.circ as structural Verilog
module sqrX (
  input  [31:0] a,
  input  [31:0] b,
  input  [31:0] c,
  input  [31:0] d,
  output [31:0] a_prime,
  output [31:0] b_prime,
  output [31:0] c_prime,
  output [31:0] d_prime
);

  wire [31:0] multiplier_1_out, multiplier_2_out, multiplier_3_out, multiplier_4_out, multiplier_5_out,
       multiplier_6_out, multiplier_7_out;

  Multiplier #(.width(32)) multiplier_1 (.a(a), .b(a), .out(multiplier_1_out), .cin({32{1'b0}}));  // open: cout
  Multiplier #(.width(32)) multiplier_2 (.a(a), .b(b), .out(multiplier_2_out), .cin({32{1'b0}}));  // open: cout
  Multiplier #(.width(32)) multiplier_3 (.a(b), .b(c), .out(multiplier_3_out), .cin({32{1'b0}}));  // open: cout
  Multiplier #(.width(32)) multiplier_4 (.a(a), .b(c), .out(multiplier_4_out), .cin({32{1'b0}}));  // open: cout
  Multiplier #(.width(32)) multiplier_5 (.a(c), .b(d), .out(multiplier_5_out), .cin({32{1'b0}}));  // open: cout
  Multiplier #(.width(32)) multiplier_6 (.a(b), .b(d), .out(multiplier_6_out), .cin({32{1'b0}}));  // open: cout
  Multiplier #(.width(32)) multiplier_7 (.a(d), .b(d), .out(multiplier_7_out), .cin({32{1'b0}}));  // open: cout
  Adder #(.width(32)) adder_1 (.a(multiplier_4_out), .b(multiplier_5_out), .out(c_prime), .cin(1'b0));  // open: cout
  Adder #(.width(32)) adder_2 (.a(multiplier_3_out), .b(multiplier_7_out), .out(d_prime), .cin(1'b0));  // open: cout
  Adder #(.width(32)) adder_3 (.a(multiplier_1_out), .b(multiplier_3_out), .out(a_prime), .cin(1'b0));  // open: cout
  Adder #(.width(32)) adder_4 (.a(multiplier_2_out), .b(multiplier_6_out), .out(b_prime), .cin(1'b0));  // open: cout
endmodule

module sqrX_A (
  input  [31:0] a,
  input  [31:0] b,
  input  [31:0] c,
  input  [31:0] d,
  output [31:0] a_prime,
  output [31:0] b_prime,
  output [31:0] c_prime,
  output [31:0] d_prime
);

  wire [31:0] adder_2_out, adder_3_out, multiplier_1_out, multiplier_2_out, multiplier_3_out,
       multiplier_4_out, multiplier_5_out, multiplier_6_out, multiplier_7_out;

  Multiplier #(.width(32)) multiplier_1 (.a(a), .b(b), .out(multiplier_1_out), .cin({32{1'b0}}));  // open: cout
  Multiplier #(.width(32)) multiplier_2 (.a(a), .b(a), .out(multiplier_2_out), .cin({32{1'b0}}));  // open: cout
  Multiplier #(.width(32)) multiplier_3 (.a(b), .b(d), .out(multiplier_3_out), .cin({32{1'b0}}));  // open: cout
  Multiplier #(.width(32)) multiplier_4 (.a(b), .b(c), .out(multiplier_4_out), .cin({32{1'b0}}));  // open: cout
  Multiplier #(.width(32)) multiplier_5 (.a(a), .b(c), .out(multiplier_5_out), .cin({32{1'b0}}));  // open: cout
  Multiplier #(.width(32)) multiplier_6 (.a(c), .b(d), .out(multiplier_6_out), .cin({32{1'b0}}));  // open: cout
  Multiplier #(.width(32)) multiplier_7 (.a(d), .b(d), .out(multiplier_7_out), .cin({32{1'b0}}));  // open: cout
  Adder #(.width(32)) adder_1 (.a(multiplier_4_out), .b(multiplier_7_out), .out(c_prime), .cin(1'b0));  // open: cout
  Adder #(.width(32)) adder_2 (
    .a(multiplier_2_out), .b(multiplier_4_out), .out(adder_2_out), .cin(1'b0));  // open: cout
  Adder #(.width(32)) adder_3 (
    .a(multiplier_5_out), .b(multiplier_6_out), .out(adder_3_out), .cin(1'b0));  // open: cout
  Adder #(.width(32)) adder_4 (.a(multiplier_1_out), .b(multiplier_3_out), .out(a_prime), .cin(1'b0));  // open: cout
  Adder #(.width(32)) adder_5 (.a(c_prime), .b(adder_3_out), .out(d_prime), .cin(1'b0));  // open: cout
  Adder #(.width(32)) adder_6 (.a(a_prime), .b(adder_2_out), .out(b_prime), .cin(1'b0));  // open: cout
endmodule

module \Fibonacci数显示模块  (
  input  [31:0] in_1,
  output [3:0] out_2,
  output [3:0] out_3,
  output [3:0] out_4,
  output [3:0] out_5,
  output [3:0] out_6,
  output [3:0] out_7,
  output [3:0] out_8,
  output [3:0] out_9,
  output [3:0] out_10,
  output [3:0] out_11
);

  wire [27:0] divider_8_out;
  wire [31:0] divider_1_rem, divider_2_rem, divider_3_rem, divider_4_rem, divider_5_rem, divider_6_rem,
       divider_7_rem, divider_8_rem;
  wire [31:4] divider_1_out, divider_2_out, divider_3_out, divider_4_out, divider_5_out, divider_6_out,
       divider_7_out, divider_9_out, divider_9_rem;

  Divider #(.width(32)) divider_1 (
    .a(in_1), .b(32'h3b9aca00), .out({divider_1_out, out_2}), .rem(divider_1_rem));  // open: upper
  Divider #(.width(32)) divider_2 (
    .a(divider_1_rem), .b(32'h5f5e100), .out({divider_2_out, out_3}), .rem(divider_2_rem));  // open: upper
  Divider #(.width(32)) divider_3 (
    .a(divider_2_rem), .b(32'h989680), .out({divider_3_out, out_4}), .rem(divider_3_rem));  // open: upper
  Divider #(.width(32)) divider_4 (
    .a(divider_3_rem), .b(32'hf4240), .out({divider_4_out, out_5}), .rem(divider_4_rem));  // open: upper
  Divider #(.width(32)) divider_5 (
    .a(divider_4_rem), .b(32'h186a0), .out({divider_5_out, out_6}), .rem(divider_5_rem));  // open: upper
  Divider #(.width(32)) divider_6 (
    .a(divider_5_rem), .b(32'h2710), .out({divider_6_out, out_7}), .rem(divider_6_rem));  // open: upper
  Divider #(.width(32)) divider_7 (
    .a(divider_6_rem), .b(32'h3e8), .out({divider_7_out, out_8}), .rem(divider_7_rem));  // open: upper
  Divider #(.width(32)) divider_8 (
    .a(divider_7_rem), .b(32'h64), .out({divider_8_out, out_9}), .rem(divider_8_rem));  // open: upper
  Divider #(.width(32)) divider_9 (
    .a(divider_8_rem), .b(32'ha), .out({divider_9_out, out_10}), .rem({divider_9_rem, out_11}));  // open: upper
endmodule
